# Fritzing sketch wiring (saved by Fritzing 0.9.8b)
breadboards: 1

parts:
  128x32_OLED_FeatherWing = Adafruit OLED FeatherWing [part_number="Adafruit #2900"]
  QT_Py = Adafruit QT Py [part_number="Adafruit #4600"]
  To_TDS_Sensor = JST-VHR-3N [part_number=JST-VHR-3N package=THT]

nets (from the schematic view):
  GND: 128x32_OLED_FeatherWing.GND, QT_Py.GND, To_TDS_Sensor.pin2, To_TDS_Sensor.pin_5
  N1: 128x32_OLED_FeatherWing.SCL, QT_Py.SCL
  3.3V: 128x32_OLED_FeatherWing.3.3V, QT_Py.3.3V, To_TDS_Sensor.pin1, To_TDS_Sensor.pin_4
  N2: 128x32_OLED_FeatherWing.SDA, QT_Py.SDA
  N3: QT_Py.MISO, To_TDS_Sensor.pin3, To_TDS_Sensor.pin_6

custom parts:
  Adafruit OLED FeatherWing: This is the FeatherWing OLED: it adds a 128x32 monochrome OLED plus 3 user buttons to any Feather main board. These displays are small, only about 1" diagonal, but very readable due to the high contrast of an OLED display. This screen is made of 128x32 individual white OLED pixels and because the display makes its own light, no backlight is required. This reduces the power required to run the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
  Adafruit QT Py: What a cutie pie! Or is it... a QT Py? This diminutive dev board comes with our favorite lil chip, the SAMD21 (as made famous in our GEMMA M0 and Trinket M0 boards). This time it comes with our favorite connector - the STEMMA QT, a chainable I2C port that can be used with any of our STEMMA QT sensors and accessories. OLEDs! Inertial Measurment Units! Sensors a-plenty. All plug-and-play thanks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
